# Fritzing sketch accelerometer (saved by Fritzing 0.9.3b)
breadboards: 1

parts:
  MCU1 = Raspberry Pi Zero
  Part1 = IMU Digital Combo Board 6DOF

nets:
  N1: MCU1.pin_1, Part1.3.3V
  N2: MCU1.pin_3, Part1.SDA
  N3: MCU1.pin_5, Part1.SCL
  N4: MCU1.pin_6, Part1.GND
