# Fritzing sketch basic_circuit_pull_down_resistor (saved by Fritzing 0.9.3b)
breadboards: 1

parts:
  R1 = Resistor [tolerance=±5% resistance=220 package=THT]
  MCU1 = Raspberry Pi Zero
  S1 = Pushbutton [package="[SMD]"]
  R2 = Resistor [tolerance=±5% resistance=10k package=THT]

nets:
  N1: R1.Pin_0, S1.Pin_1, S1.Pin_2
  N2: R1.Pin_1, MCU1.pin_1
  N3: MCU1.pin_25, R2.Pin_0
  N4: MCU1.pin_31, R2.Pin_1
