# Fritzing sketch blinking-led (saved by Fritzing 0.9.3b)
breadboards: 1

parts:
  LED1 = LED - 5mm [color="Red (633nm)" package="5 mm [THT]"]
  R1 = Resistor [tolerance=±5% resistance=220 package=THT]
  MCU1 = Raspberry Pi Zero

nets:
  N1: LED1.cathode, MCU1.pin_11
  N2: LED1.anode, R1.Pin_1
  N3: R1.Pin_0, MCU1.pin_1
