# Fritzing sketch flowing_leds (saved by Fritzing 0.9.3b)
breadboards: 1

parts:
  MCU1 = Raspberry Pi Zero
  LED1 = LED - 5mm [color="Red (633nm)" package="5 mm [THT]"]
  LED2 = LED - 5mm [color="Red (633nm)" package="5 mm [THT]"]
  LED3 = LED - 5mm [color="Red (633nm)" package="5 mm [THT]"]
  LED4 = LED - 5mm [color="Red (633nm)" package="5 mm [THT]"]
  LED5 = LED - 5mm [color="Red (633nm)" package="5 mm [THT]"]
  LED6 = LED - 5mm [color="Red (633nm)" package="5 mm [THT]"]
  LED7 = LED - 5mm [color="Red (633nm)" package="5 mm [THT]"]
  LED8 = LED - 5mm [color="Red (633nm)" package="5 mm [THT]"]
  R1 = Resistor [tolerance=±5% resistance=220 package=THT]
  R2 = Resistor [tolerance=±5% resistance=220 package=THT]
  R3 = Resistor [tolerance=±5% resistance=220 package=THT]
  R4 = Resistor [tolerance=±5% resistance=220 package=THT]
  R5 = Resistor [tolerance=±5% resistance=220 package=THT]
  R6 = Resistor [tolerance=±5% resistance=220 package=THT]
  R7 = Resistor [tolerance=±5% resistance=220 package=THT]
  R8 = Resistor [tolerance=±5% resistance=220 package=THT]

nets:
  N1: MCU1.pin_1, MCU1.pin_17, R2.Pin_0, R3.Pin_0, R4.Pin_0, R5.Pin_0, R6.Pin_0, R7.Pin_0, R8.Pin_0
  N2: MCU1.pin_7, LED8.cathode
  N3: MCU1.pin_11, LED4.cathode
  N4: MCU1.pin_12, LED7.cathode
  N5: MCU1.pin_13, LED6.cathode
  N6: MCU1.pin_15, LED5.cathode
  N7: MCU1.pin_16, LED3.cathode
  N8: MCU1.pin_18, LED1.cathode
  N9: MCU1.pin_22, LED2.cathode
  N10: LED1.anode, R4.Pin_1
  N11: LED2.anode, R3.Pin_1
  N12: LED3.anode, R5.Pin_1
  N13: LED4.anode, R1.Pin_1
  N14: LED5.anode, R6.Pin_1
  N15: LED6.anode, R7.Pin_1
  N16: LED7.anode, R8.Pin_1
  N17: LED8.anode, R2.Pin_1
