# Fritzing sketch push_button_led (saved by Fritzing 0.9.3b)
breadboards: 1

parts:
  R1 = Resistor [tolerance=±5% resistance=220 package=THT]
  MCU1 = Raspberry Pi Zero
  S1 = Pushbutton [package="[SMD]"]  # not connected
  LED1 = LED - 5mm [color="Red (633nm)" package="5 mm [THT]"]

nets:
  N1: R1.Pin_0, LED1.anode
  N2: R1.Pin_1, MCU1.pin_1
  N3: MCU1.pin_11, LED1.cathode
