# Fritzing sketch rgb_led (saved by Fritzing 0.9.3b)
breadboards: 1

parts:
  MCU1 = Raspberry Pi Zero
  R1 = Resistor [tolerance=±5% resistance=220 package=THT]
  R2 = Resistor [tolerance=±5% resistance=220 package=THT]
  R3 = Resistor [tolerance=±5% resistance=220 package=THT]
  LED1 = RGB LED (com. cathode, rgb) [package="5 mm [THT]"]

nets:
  N1: MCU1.pin_6, MCU1.pin_9, LED1.common_cathode
  N2: MCU1.pin_11, R3.Pin_0
  N3: MCU1.pin_12, R2.Pin_0
  N4: MCU1.pin_13, R1.Pin_0
  N5: R1.Pin_1, LED1.blue_anode
  N6: R2.Pin_1, LED1.green_anode
  N7: R3.Pin_1, LED1.red_anode
