# Fritzing sketch seven_segment (saved by Fritzing 0.9.3b)
breadboards: 1

parts:
  MCU1 = Raspberry Pi Zero
  R2 = Resistor [tolerance=±5% resistance=220 package=THT]
  U1 = 74HC595 SMD [package="SO16 [SMD]"]
  U2 = 7-SEGMENT-DISPLAY [package=7-segment-display]

nets:
  N1: MCU1.pin_2, U1.MR, U1.VCC
  N2: MCU1.pin_6, MCU1.pin_9, MCU1.pin_34, MCU1.pin_39, R2.Pin_0, U1.GND
  N3: MCU1.pin_11, U1.DS
  N4: MCU1.pin_12, U1.ST_CP
  N5: MCU1.pin_13, U1.SH_CP
  N6: R2.Pin_1, U2.C
  N7: U1.Q1, U2.A
  N8: U1.Q2, U2.DP
  N9: U1.Q3, U2.G1
  N10: U1.Q4, U2.D
  N11: U1.Q5, U2.G
  N12: U1.Q6, U2.E
  N13: U1.Q7, U2.B
  N14: U1.Q0, U2.G2
