# Fritzing sketch shift_register (saved by Fritzing 0.9.3b)
breadboards: 1

parts:
  MCU1 = Raspberry Pi Zero
  LED1 = LED - 5mm [color="Red (633nm)" package="5 mm [THT]"]
  LED2 = LED - 5mm [color="Red (633nm)" package="5 mm [THT]"]
  LED3 = LED - 5mm [color="Red (633nm)" package="5 mm [THT]"]
  LED4 = LED - 5mm [color="Red (633nm)" package="5 mm [THT]"]
  LED5 = LED - 5mm [color="Red (633nm)" package="5 mm [THT]"]
  LED6 = LED - 5mm [color="Red (633nm)" package="5 mm [THT]"]
  LED7 = LED - 5mm [color="Red (633nm)" package="5 mm [THT]"]
  LED8 = LED - 5mm [color="Red (633nm)" package="5 mm [THT]"]
  R1 = Resistor [tolerance=±5% resistance=220 package=THT]
  R2 = Resistor [tolerance=±5% resistance=220 package=THT]
  R3 = Resistor [tolerance=±5% resistance=220 package=THT]
  R4 = Resistor [tolerance=±5% resistance=220 package=THT]
  R5 = Resistor [tolerance=±5% resistance=220 package=THT]
  R6 = Resistor [tolerance=±5% resistance=220 package=THT]
  R7 = Resistor [tolerance=±5% resistance=220 package=THT]
  R8 = Resistor [tolerance=±5% resistance=220 package=THT]
  U1 = 74HC595 SMD [package="SO16 [SMD]"]

nets:
  N1: MCU1.pin_2, U1.MR, U1.VCC
  N2: MCU1.pin_11, U1.DS
  N3: MCU1.pin_12, U1.ST_CP
  N4: MCU1.pin_13, U1.SH_CP
  N5: LED1.cathode, LED2.cathode, LED3.cathode, LED4.cathode, LED5.cathode, LED6.cathode, LED7.cathode, LED8.cathode, R5.Pin_1, R8.Pin_1, U1.GND, U1.OE
  N6: LED2.anode, R3.Pin_1
  N7: LED3.anode, R6.Pin_1
  N8: LED6.anode, R1.Pin_1
  N9: LED8.anode, R2.Pin_1
  N10: R1.Pin_0, U1.Q0
  N11: R2.Pin_0, U1.Q7
  N12: R3.Pin_0, U1.Q6
  N13: R4.Pin_0, U1.Q5
  N14: R5.Pin_0, U1.Q4
  N15: R6.Pin_0, U1.Q3
  N16: R7.Pin_0, U1.Q2
  N17: R8.Pin_0, U1.Q1
